# Fritzing sketch cam shield v8 (saved by Fritzing 0.9.5d)
circuit board: 2.8cm x 3.8cm
perfboards: 1

parts:
  U1 = Voltage Regulator - 5V [package="TO220 [THT]"]
  POWER = female pin header, 3 pins [form="♀ (female)"]
  SERVO = female pin header, 4 pins [form="♀ (female)"]
  2K = Resistor [tolerance=±5% resistance=220 package=THT]
  2K_2 = Resistor [tolerance=±5% resistance=220 package=THT]
  1K = Resistor [tolerance=±5% resistance=220 package=THT]
  1K_2 = Resistor [tolerance=±5% resistance=1k package=THT]
  Cout = Ceramic Capacitor [capacitance=100nF package="200 mil [THT, multilayer]"]
  Cout_2 = Ceramic Capacitor [capacitance=100nF package="200 mil [THT, multilayer]"]
  ESP32CAM = ESP32 - CAM
  Cin = Ceramic Capacitor [capacitance=100nF package="200 mil [THT, multilayer]"]

nets:
  N1: U1.input_voltage, SERVO.pin1, Cin.1
  GND: U1.GND, POWER.pin3, SERVO.pin4, 1K.Pin_1, 1K_2.Pin_1, Cout.0, Cout_2.0, ESP32CAM.GND, Cin.0
  N2: U1.output_voltage, POWER.pin2, Cout.1, Cout_2.1, ESP32CAM.5V
  N3: POWER.pin1, ESP32CAM.IO12
  N4: SERVO.pin2, 2K_2.Pin_0
  N5: SERVO.pin3, 2K.Pin_0
  N6: 2K.Pin_1, ESP32CAM.IO14
  N7: 2K_2.Pin_1, ESP32CAM.IO15

notes:
  GND C1 C2 V+
  GND 5V PWM
  -          +
  -     +
  V+ GND 5V

custom parts:
  ESP32 - CAM: The ESP32-CAM has a very competitive small-size camera module that can operate independently as a minimum system with a footprint of only 27*40.5*4.5mm and a deep sleep current of up to 6mA.
